# Fritzing sketch goldibox (saved by Fritzing 0.9.2b)
circuit board: 4cm x 2.5cm
perfboards: 1

parts:
  J1_Peltier = Peltier Element
  F1_Fan_12VDC = Fan - Ventilador [package=THT]
  R16 = Resistor [tolerance=±5% resistance=4.7k package=THT]
  R17 = Resistor [tolerance=±5% resistance=1k package=THT]
  C16 = Electrolytic Capacitor [capacitance=10µF package="100 mil [THT, electrolytic]"]
  Therm1_int = Temperature Sensor (Thermistor) [thermistor_type=NTC package=THT]
  R19 = Resistor [tolerance=±5% resistance=4.7k package=THT]
  R20 = Resistor [tolerance=±5% resistance=1k package=THT]
  C17 = Electrolytic Capacitor [capacitance=10µF package="100 mil [THT, electrolytic]"]
  Therm2_ext = Temperature Sensor (Thermistor) [thermistor_type=NTC package=THT]
  C23 = Ceramic Capacitor [capacitance=100nF voltage=20V package="100 mil [THT, multilayer]"]
  C24 = Ceramic Capacitor [capacitance=100nF package="100 mil [THT, multilayer]"]
  Part2 = IRF540 MOSFET module
  PocketBeagle = PocketBeagle
  J1 = male pin header, 2 pins [form="♂ (male)"]
  J2 = female pin header, 2 pins [form="♀ (female)"]
  J3 = male pin header, 2 pins [form="♂ (male)"]
  J15 = male pin header, 1 pin [form="♂ (male)"]
  J16 = female pin header, 1 pin [form="♀ (female)"]
  J10 = female pin header, 1 pin [form="♀ (female)"]
  J12 = female pin header, 1 pin [form="♀ (female)"]
  J11 = female pin header, 1 pin [form="♀ (female)"]
  J4 = female pin header, 2 pins [form="♀ (female)"]
  J18 = female pin header, 3 pins [form="♀ (female)"]
  J19 = female pin header, 6 pins [form="♀ (female)"]
  S2_** = H-Bridge with L298N v2
  J20 = male pin header, 3 pins [form="♂ (male)"]
  J14 = male pin header, 4 pins [form="♂ (male)"]
  J13 = female pin header, 4 pins [form="♀ (female)"]
  J8 = female alternating pin header, 3 pins [form="♀ (female)"]
  J7 = male pin header, 3 pins [form="♂ (male)"]
  J9 = male pin header, 3 pins [form="♂ (male)"]
  J21 = male pin header, 6 pins [form="♂ (male)"]
  J22 = male pin header, 1 pin [form="♂ (male)"]
  J22_2 = male pin header, 2 pins [form="♂ (male)"]

nets:
  N1: J1_Peltier.pin1, S2_**.OUT2, S2_**.OUT3
  N2: J1_Peltier.pin2, S2_**.OUT1, S2_**.OUT4
  N3: F1_Fan_12VDC.5V, Part2.Vout+
  N4: F1_Fan_12VDC.GND, Part2.Vout-
  N5: R16.Pin_0, R17.Pin_0, J1.pin1
  N6: R16.Pin_1, C16.+, C24.1, J14.pin3
  N7: R17.Pin_1, R20.Pin_1, J14.pin1
  N8: C16.-, C17.-, C23.0, C24.0, J1.pin2, J3.pin2, J14.pin2
  N9: Therm1_int.pin_0, J2.pin1
  N10: Therm1_int.pin_1, J2.pin2
  N11: R19.Pin_0, R20.Pin_0, J3.pin1
  N12: R19.Pin_1, C17.+, C23.1, J14.pin4
  N13: Therm2_ext.pin_0, J4.pin1
  N14: Therm2_ext.pin_1, J4.pin2
  5V: Part2.V+, J16.pin1, S2_**.+VSS
  GND: Part2.V-, Part2.Vin-, PocketBeagle.GND, J10.pin1, S2_**.GND, J9.pin1, J21.pin6, J22.pin1
  FAN: Part2.S, J12.pin1
  12V: Part2.Vin+, S2_**.+VS
  N15: PocketBeagle.VIN, J15.pin1
  N16: PocketBeagle.AIN6/GPIO87, J20.pin1
  N17: PocketBeagle.GPIO89, J20.pin2
  N18: PocketBeagle.USB1.VBUS, J21.pin1
  ENA/B: PocketBeagle.SPI0.CS, J20.pin3
  N19: PocketBeagle.USB1.VIN, J21.pin2
  N20: PocketBeagle.USB1.DN, J21.pin3
  N21: PocketBeagle.USB1.DP, J21.pin4
  N22: PocketBeagle.USB1.ID, J21.pin5
  N23: PocketBeagle.AIN.VREFN, J7.pin1
  N24: PocketBeagle.AIN.VREFP, J9.pin2
  N25: PocketBeagle.AIN0(1.8V), J7.pin2
  N26: PocketBeagle.GPIO20, J9.pin3
  N27: PocketBeagle.AIN1(1.8V), J7.pin3
  N28: PocketBeagle.UART0.TX, J22_2.pin1
  N29: PocketBeagle.UART0.RX, J22_2.pin2
  N30: J11.pin1, J13.pin1
  N31: J18.pin1, J19.pin3, J19.pin4
  N32: J18.pin2, J19.pin2, J19.pin5
  N33: J18.pin3, J19.pin1, J19.pin6
  N34: J13.pin2, J8.pin1
  N35: J13.pin3, J8.pin2
  N36: J13.pin4, J8.pin3

notes:
  Configure both L298N 2A bridges in parallel for 4A Peltier
  Goldibox, Not too hot, not too cold.  See https://github.com/zultron/goldibox, 0.1
  ** onboard 5V reg
  12VDC in
  USB breakout
  optional serial
  console
  for WiFi

custom parts:
  Fan - Ventilador: Ventilador de 2 pines, se encuentra comunmente en computadoras de escritorio
  H-Bridge with L298N v2: h-bridge
