# Fritzing sketch incubator (saved by Fritzing 0.9.2b)
circuit board: 4cm x 3.23893cm
perfboards: 1

parts:
  J1_Peltier = Peltier Element
  F1_Fan_12VDC = Fan - Ventilador [package=THT]
  R16 = Resistor [tolerance=±5% resistance=4.7k package=THT]
  R17 = Resistor [tolerance=±5% resistance=2.0k package=THT]
  C16 = Electrolytic Capacitor [capacitance=10µF package="100 mil [THT, electrolytic]"]
  100k_Therm1 = Temperature Sensor (Thermistor) [thermistor_type=NTC package=THT]
  R19 = Resistor [tolerance=±5% resistance=4.7k package=THT]
  R20 = Resistor [tolerance=±5% resistance=2.0k package=THT]
  C17 = Electrolytic Capacitor [capacitance=10µF package="100 mil [THT, electrolytic]"]
  100k_Therm2 = Temperature Sensor (Thermistor) [thermistor_type=NTC package=THT]
  R22 = Resistor [tolerance=±5% resistance=4.7k package=THT]
  R23 = Resistor [tolerance=±5% resistance=2.0k package=THT]
  C19 = Electrolytic Capacitor [capacitance=10µF package="100 mil [THT, electrolytic]"]
  100k_Therm3 = Temperature Sensor (Thermistor) [thermistor_type=NTC package=THT]
  C23 = Ceramic Capacitor [capacitance=100nF voltage=20V package="100 mil [THT, multilayer]"]
  C24 = Ceramic Capacitor [capacitance=100nF package="100 mil [THT, multilayer]"]
  C25 = Ceramic Capacitor [capacitance=100nF package="100 mil [THT, multilayer]"]
  Part2 = IRF540 MOSFET module
  PocketBeagle = PocketBeagle
  J1 = male pin header, 2 pins [form="♂ (male)"]
  J2 = female pin header, 2 pins [form="♀ (female)"]
  J3 = male pin header, 2 pins [form="♂ (male)"]
  J6 = female pin header, 2 pins [form="♀ (female)"]
  J5 = male pin header, 2 pins [form="♂ (male)"]
  J14 = male pin header, 5 pins [form="♂ (male)"]
  J13 = female pin header, 5 pins [form="♀ (female)"]
  J15 = male pin header, 1 pin [form="♂ (male)"]
  J16 = female pin header, 1 pin [form="♀ (female)"]
  J17 = male pin header, 3 pins [form="♂ (male)"]
  J12 = female pin header, 1 pin [form="♀ (female)"]
  J11 = female pin header, 1 pin [form="♀ (female)"]
  J7 = male pin header, 4 pins [form="♂ (male)"]
  J9 = male pin header, 3 pins [form="♂ (male)"]
  J8 = female pin header, 4 pins [form="♀ (female)"]
  J10 = female pin header, 1 pin [form="♀ (female)"]
  J4 = female pin header, 2 pins [form="♀ (female)"]
  J18 = female pin header, 3 pins [form="♀ (female)"]
  J19 = female pin header, 6 pins [form="♀ (female)"]
  S2_** = H-Bridge with L298N v2

nets:
  N1: J1_Peltier.pin1, S2_**.OUT2, S2_**.OUT3
  N2: J1_Peltier.pin2, S2_**.OUT1, S2_**.OUT4
  N3: F1_Fan_12VDC.5V, Part2.Vout+
  N4: F1_Fan_12VDC.GND, Part2.Vout-
  N5: R16.Pin_0, R17.Pin_0, J1.pin1
  N6: R16.Pin_1, C16.+, C24.1, J14.pin3
  N7: R17.Pin_1, R20.Pin_1, R23.Pin_1, J14.pin1
  N8: C16.-, C17.-, C19.-, C23.0, C24.0, C25.0, J1.pin2, J3.pin2, J5.pin2, J14.pin2
  N9: 100k_Therm1.pin_0, J2.pin1
  N10: 100k_Therm1.pin_1, J2.pin2
  N11: R19.Pin_0, R20.Pin_0, J3.pin1
  N12: R19.Pin_1, C17.+, C23.1, J14.pin4
  N13: 100k_Therm2.pin_0, J4.pin1
  N14: 100k_Therm2.pin_1, J4.pin2
  N15: R22.Pin_0, R23.Pin_0, J5.pin1
  N16: R22.Pin_1, C19.+, C25.1, J14.pin5
  N17: 100k_Therm3.pin_0, J6.pin1
  N18: 100k_Therm3.pin_1, J6.pin2
  5V: Part2.V+, J16.pin1, S2_**.+VSS
  GND: Part2.V-, Part2.Vin-, PocketBeagle.GND, J12.pin1, J9.pin3, S2_**.GND
  FAN: Part2.S, J11.pin1
  12V: Part2.Vin+, S2_**.+VS
  N19: PocketBeagle.VIN, J15.pin1
  N20: PocketBeagle.AIN.VREFN, J7.pin1
  N21: PocketBeagle.AIN.VREFP, J9.pin1
  N22: PocketBeagle.AIN0(1.8V), J7.pin2
  N23: PocketBeagle.GPIO20, J9.pin2
  N24: PocketBeagle.AIN1(1.8V), J7.pin3
  N25: PocketBeagle.AIN2(1.8V), J7.pin4
  N26: PocketBeagle.GPIO59, J17.pin1
  N27: PocketBeagle.GPIO58, J17.pin2
  N28: PocketBeagle.GPIO57, J17.pin3
  N29: J13.pin1, J10.pin1
  N30: J13.pin2, J8.pin1
  N31: J13.pin3, J8.pin2
  N32: J13.pin4, J8.pin3
  N33: J13.pin5, J8.pin4
  N34: J18.pin1, J19.pin1, J19.pin6
  N35: J18.pin2, J19.pin2, J19.pin5
  N36: J18.pin3, J19.pin3, J19.pin4

notes:
  Configure both L298N 2A bridges in parallel for 4A Peltier
  Only Therm1 in use; others for future expansion
  Goldilocks Incubator, Not too hot, not too cold.  See https://github.com/zultron/goldilocks-incubator, 0.1
  ** onboard 5V reg
  12VDC in

custom parts:
  Fan - Ventilador: Ventilador de 2 pines, se encuentra comunmente en computadoras de escritorio
  H-Bridge with L298N v2: h-bridge
